# Fritzing sketch UV_sensor_diagrams (saved by Fritzing 1.0.0rc)
circuit board: 2.84438cm x 2.16081cm

parts:
  UV_Sensor = GUVA-S12SD UV Light Sensor [part_number=GUVA-S12SD]
  C1 = Ceramic Capacitor [capacitance="100 nF" voltage=35V package="0805 [SMD, multilayer]"]
  LED_G1 = smd LED [color="Green (565nm)" current=0A package="0805 [SMD]"]
  R2 = Resistor [tolerance=±5% resistance=220 package="0805 [SMD]"]
  R3 = Resistor [tolerance=±5% resistance=220 package="0805 [SMD]"]
  R5 = Resistor [tolerance=±5% resistance=220 package="0805 [SMD]"]
  R6 = Resistor [tolerance=±5% resistance=220 package="0805 [SMD]"]
  R7 = Resistor [tolerance=±5% resistance=220 package="0805 [SMD]"]
  R1 = Resistor [tolerance=±5% resistance=220 package="0805 [SMD]"]
  LED_Y1 = smd LED [color="Yellow (585nm)" package="0805 [SMD]"]
  LED_R1 = smd LED [color="Red (633nm)" package="0805 [SMD]"]
  LED_B1 = smd LED [color="Blue (505nm)" package="0805 [SMD]"]
  R4 = Resistor [tolerance=±5% resistance=220 package="0805 [SMD]"]
  LED_G2 = smd LED [color="Green (565nm)" package="0805 [SMD]"]
  LED_R2 = smd LED [color="Red (633nm)" package="0805 [SMD]"]
  LED_Y2 = smd LED [color="Yellow (585nm)" package="0805 [SMD]"]
  U2 = 74HC595 SMD [package="SO16 [SMD]"]
  Microcontroller = Adafruit Trinket M0 [part_number="Adafruit #3500"]

nets:
  5V: UV_Sensor.5V, C1.1, U2.MR, U2.VCC, Microcontroller.3.3V
  N1: UV_Sensor.Out, Microcontroller.D1_A0_PA02
  GND: UV_Sensor.GND, C1.0, LED_G1.anode, LED_Y1.anode, LED_R1.anode, LED_B1.anode, LED_G2.anode, LED_R2.anode, LED_Y2.anode, U2.GND, U2.OE, Microcontroller.GND
  N2: LED_G1.cathode, R1.Pin_1
  N3: R2.Pin_0, U2.Q2
  N4: R2.Pin_1, LED_G2.cathode
  N5: R3.Pin_0, U2.Q3
  N6: R3.Pin_1, LED_Y1.cathode
  N7: R5.Pin_0, U2.Q5
  N8: R5.Pin_1, LED_R1.cathode
  N9: R6.Pin_0, U2.Q6
  N10: R6.Pin_1, LED_R2.cathode
  N11: R7.Pin_0, U2.Q7
  N12: R7.Pin_1, LED_B1.cathode
  N13: R1.Pin_0, U2.Q1
  N14: R4.Pin_0, U2.Q4
  N15: R4.Pin_1, LED_Y2.cathode
  N16: U2.SH_CP, Microcontroller.D3_A3_PA07_RXD_SCK
  N17: U2.ST_CP, Microcontroller.D0_A4_PA08_SDA
  N18: U2.DS, Microcontroller.D4_A2_PA06_TXD_MOSI

custom parts:
  GUVA-S12SD UV Light Sensor: Extend your light-sensing spectrum with this analog UV sensor module. It uses a UV photodiode, which can detect the 240-370nm range of light (which covers UVB and most of UVA spectrum). The signal level from the photodiode is very small, in the nano-ampere level, so we tossed on an opamp to amplify the signal to a more manageable volt-level.
